# Fritzing sketch Connections-Sketch (saved by Fritzing 0.9.2b)

parts:
  Grenier_1 = Arduino Mega 2560 (Rev3)
  Cave = Arduino Mega 2560 (Rev3)
  Raspberry_Pi1 = Raspberry Pi 2
  Grenier_2 = Arduino Mega 2560 (Rev3)

nets:
  N1: Grenier_1.D19/RX1, Raspberry_Pi1.GIPO14
  N2: Grenier_1.D18/TX1, Raspberry_Pi1.GIPO15
  N3: Grenier_1.D17_PWM/RX2, Cave.D16_PWM/TX2
  N4: Grenier_1.D16_PWM/TX2, Cave.D17_PWM/RX2
  N5: Grenier_1.D15/RX3, Grenier_2.D14/TX3
  N6: Grenier_1.D14/TX3, Grenier_2.D15/RX3
